# Fritzing sketch attiny_cartografia (saved by Fritzing 0.9.3b)
perfboards: 1

parts:
  U2 = ATTINY45 [package=dip]
  BAT1 = Battery Holders [package=battcom_20mm_pth]

nets:
  N1: U2.GND, BAT1.+
  N2: U2.VCC, BAT1.-

notes:
  A
  B
  C
  D
